// Logisim project Multiprocesador.circ as structural Verilog: 1 circuit, main circuit Main
module Main (
);

  wire Encender_MIPS, Limpiar_RAM, MIPS_Escribir, MIPS_Solicitar_RAM, not_1_out, Poder, Reloj,
       Usar_Little_Endian;
  wire [7:0] RAM_Byte;
  wire [15:0] RAM_Nibble;
  wire [31:0] MIPS_Direccion_RAM, MIPS_Entrada_RAM, MIPS_Indice_Instruccion, RAM_Word, ROM_Word;

  // DipSwitch #(.number(3)) Opciones: pin names not known; wires that end beside it: Limpiar_RAM, Usar_Little_Endian, Poder
  Button u_Encender_MIPS (.out(Encender_MIPS));
  Clock u_Reloj (.out(Reloj));
  not not_1 (not_1_out, MIPS_Solicitar_RAM);
  // MIPS_Processor mips_processor_1: pin names not known; wires that end beside it: RAM_Byte, Reloj, Poder, Encender_MIPS, ROM_Word, RAM_Word, RAM_Nibble, MIPS_Indice_Instruccion, MIPS_Solicitar_RAM, MIPS_Escribir, MIPS_Direccion_RAM, MIPS_Entrada_RAM
  Four_GB_ROM_Controller four_gb_rom_controller_1 (
    .Direccion_32_bits(MIPS_Indice_Instruccion), .Usar_Litte_Endian(Usar_Little_Endian), .Word(ROM_Word));  // open: Doubleword, Nibble, Byte
  Four_GB_RAM_Controller four_gb_ram_controller_1 (
    .Reloj(Reloj), .Limpiar(Limpiar_RAM), .Bloquear(not_1_out), .Escribir(MIPS_Escribir),
    .Direccion_32_bits(MIPS_Direccion_RAM), .Usar_Litte_Endian(Usar_Little_Endian),
    .Entrada(MIPS_Entrada_RAM), .Word(RAM_Word), .Nibble(RAM_Nibble), .Byte(RAM_Byte));  // open: Doubleword

  // Notes on the sheet:
  //   Configuración
  //   Unidades de Memoria
  //   Procesadores
endmodule
