// Logisim project Main.circ as structural Verilog: 9 circuits, main circuit main
module main (
);

  wire clock_1_out, Dormir_ID, Dormir_IF, ID_Tipo_I, ID_Tipo_J, ID_Tipo_R, instruction_decoder_1_tipo_i,
       instruction_decoder_1_tipo_j, instruction_decoder_1_tipo_r, not_1_out, Primer_Ciclo, Reiniciar_ID,
       Reiniciar_IF, Reloj, switch_1_p2, Tomar_Salto, Usar_Little_Endian;
  wire [4:0] ID_Cantidad_Corrimiento, ID_Registro_Destino, ID_Registro_Fuente, ID_Registro_Objetivo,
       instruction_decoder_1_cantidad_corrimiento, instruction_decoder_1_registro_destino,
       instruction_decoder_1_registro_fuente, instruction_decoder_1_registro_objetivo;
  wire [6:0] ID_Funcion_Aritmetica, instruction_decoder_1_funcion_aritmetica;
  wire [15:0] ID_Valor_Inmediato, instruction_decoder_1_valor_inmediato;
  wire [25:0] ID_Direccion_Inmediata, instruction_decoder_1_direccion_inmediata;
  wire [31:0] four_gb_rom_controller_1_word, IF_Indice_Instruccion, IF_Instruccion, Indice_Salto,
       pc_controller_1_indice_siguiente;

  // Switch switch_1: pin names not known; wires that end beside it: 1'b1, switch_1_p2
  Pull_Resistor pull_resistor_1 (.node(switch_1_p2));
  Clock clock_1 (.out(clock_1_out));
  Instruction_Decoder instruction_decoder_1 (
    .Instruccion(IF_Instruccion), .Funcion_Aritmetica(instruction_decoder_1_funcion_aritmetica),
    .Cantidad_Corrimiento(instruction_decoder_1_cantidad_corrimiento),
    .Registro_Destino(instruction_decoder_1_registro_destino),
    .Valor_Inmediato(instruction_decoder_1_valor_inmediato),
    .Registro_Objetivo(instruction_decoder_1_registro_objetivo),
    .Registro_Fuente(instruction_decoder_1_registro_fuente),
    .Direccion_Inmediata(instruction_decoder_1_direccion_inmediata), .Tipo_I(instruction_decoder_1_tipo_i),
    .Tipo_J(instruction_decoder_1_tipo_j), .Tipo_R(instruction_decoder_1_tipo_r));
  Boot_Controller boot_controller_1 (
    .Reloj_Externo(clock_1_out), .Interruptor(switch_1_p2), .Primer_Ciclo(Primer_Ciclo), .Reloj(Reloj));
  PC_Controller pc_controller_1 (
    .Indice_Anterior(IF_Indice_Instruccion), .Indice_Salto(Indice_Salto), .Tomar_Salto(Tomar_Salto),
    .Indice_Siguiente(pc_controller_1_indice_siguiente));
  Four_GB_ROM_Controller four_gb_rom_controller_1 (
    .Direccion_32_bits(IF_Indice_Instruccion), .Usar_Litte_Endian(Usar_Little_Endian),
    .Word(four_gb_rom_controller_1_word));  // open: Doubleword, Nibble, Byte
  Register #(.width(7)) u_ID_Funcion_Aritmetica (
    .D(instruction_decoder_1_funcion_aritmetica), .en(Dormir_ID), .clk(Reloj), .Q(ID_Funcion_Aritmetica),
    .clr(Reiniciar_ID));
  Register #(.width(5)) u_ID_Cantidad_Corrimiento (
    .D(instruction_decoder_1_cantidad_corrimiento), .en(Dormir_ID), .clk(Reloj), .Q(ID_Cantidad_Corrimiento),
    .clr(Reiniciar_ID));
  Register #(.width(5)) u_ID_Registro_Destino (
    .D(instruction_decoder_1_registro_destino), .en(Dormir_ID), .clk(Reloj), .Q(ID_Registro_Destino),
    .clr(Reiniciar_ID));
  Register #(.width(16)) u_ID_Valor_Inmediato (
    .D(instruction_decoder_1_valor_inmediato), .en(Dormir_ID), .clk(Reloj), .Q(ID_Valor_Inmediato),
    .clr(Reiniciar_ID));
  Register #(.width(5)) u_ID_Registro_Objetivo (
    .D(instruction_decoder_1_registro_objetivo), .en(Dormir_ID), .clk(Reloj), .Q(ID_Registro_Objetivo),
    .clr(Reiniciar_ID));
  Register #(.width(5)) u_ID_Registro_Fuente (
    .D(instruction_decoder_1_registro_fuente), .en(Dormir_ID), .clk(Reloj), .Q(ID_Registro_Fuente),
    .clr(Reiniciar_ID));
  Register #(.width(26)) u_ID_Direccion_Inmediata (
    .D(instruction_decoder_1_direccion_inmediata), .en(Dormir_ID), .clk(Reloj), .Q(ID_Direccion_Inmediata),
    .clr(Reiniciar_ID));
  Register #(.width(1)) u_ID_Tipo_I (
    .D(instruction_decoder_1_tipo_i), .clk(Reloj), .Q(ID_Tipo_I), .clr(Reiniciar_ID));  // open: en
  Register #(.width(1)) u_ID_Tipo_J (
    .D(instruction_decoder_1_tipo_j), .en(Dormir_ID), .clk(Reloj), .Q(ID_Tipo_J), .clr(Reiniciar_ID));
  Register #(.width(1)) u_ID_Tipo_R (
    .D(instruction_decoder_1_tipo_r), .en(Dormir_ID), .clk(Reloj), .Q(ID_Tipo_R), .clr(Reiniciar_ID));
  // Probe on pc_controller_1_indice_siguiente
  // Probe on four_gb_rom_controller_1_word
  Register #(.width(32)) register_1 (
    .D(pc_controller_1_indice_siguiente), .en(Dormir_IF), .clk(Reloj), .Q(IF_Indice_Instruccion),
    .clr(Reiniciar_IF));
  Register #(.width(32)) u_IF_Instruccion (
    .D(four_gb_rom_controller_1_word), .en(not_1_out), .clk(Reloj), .Q(IF_Instruccion), .clr(Reiniciar_IF));
  not not_1 (not_1_out, Dormir_IF);

  // Notes on the sheet:
  //   Encender computadora
  //   Etapa I: Buscar instrucción
  //   Encender o apagar procesador
  //   Etapa II: Decodificar instrucción
endmodule

module Boot_Controller (
  input  Reloj_Externo,
  input  Interruptor,
  output Primer_Ciclo,
  output Reloj
);

  wire and_1_out, d_ff_1_q, d_ff_1_qn, not_1_out, t_ff_1_q, t_ff_1_qn;

  T_Flip_Flop t_ff_1 (
    .T(t_ff_1_qn), .clk(Reloj_Externo), .Q(t_ff_1_q), .Qn(t_ff_1_qn), .reset(not_1_out), .preset(1'b0));
  not not_1 (not_1_out, Interruptor);
  and and_1 (and_1_out, Reloj_Externo, Interruptor);
  and and_2 (Reloj, t_ff_1_q, and_1_out);
  D_Flip_Flop d_ff_1 (
    .D(t_ff_1_qn), .clk(Reloj_Externo), .Q(d_ff_1_q), .Qn(d_ff_1_qn), .preset(1'b0), .reset(not_1_out));
  // NoConnect on d_ff_1_qn
  and and_3 (Primer_Ciclo, d_ff_1_q, Reloj);
endmodule

module Four_GB_ROM_Controller (
  input  [31:0] Direccion_32_bits,
  input  Usar_Litte_Endian,
  output [63:0] Doubleword,
  output [31:0] Word,
  output [15:0] Nibble,
  output [7:0] Byte
);

  wire [2:0] subtractor_2_out;
  wire [31:0] multiplexer_1_out, subtractor_1_out;
  wire [63:0] multiplexer_2_out, multiplexer_3_out, rom_1_data, rom_2_data, rom_3_data, rom_4_data,
       rom_5_data, rom_6_data, rom_7_data, rom_8_data, rom_9_data, rom_10_data, rom_11_data, rom_12_data,
       rom_13_data, rom_14_data, rom_15_data, rom_16_data, rom_17_data, rom_18_data, rom_19_data,
       rom_20_data, rom_21_data, rom_22_data, rom_23_data, rom_24_data, rom_25_data, rom_26_data,
       rom_27_data, rom_28_data, rom_29_data, rom_30_data, rom_31_data, rom_32_data;

  Subtractor #(.width(32)) subtractor_1 (
    .a({32{1'b1}}), .b(Direccion_32_bits), .out(subtractor_1_out), .bin(1'b0));  // open: bout
  Multiplexer #(.width(32)) multiplexer_1 (
    .in0(Direccion_32_bits), .in1(subtractor_1_out), .out(multiplexer_1_out), .sel(Usar_Litte_Endian));
  Subtractor #(.width(3)) subtractor_2 (
    .a(3'b111), .b(multiplexer_1_out[2:0]), .out(subtractor_2_out), .bin(1'b0));  // open: bout
  ROM #(.addrWidth(24), .dataWidth(64)) rom_1 (.addr(multiplexer_1_out[26:3]), .data(rom_1_data));
  ROM #(.addrWidth(24), .dataWidth(64)) rom_2 (.addr(multiplexer_1_out[26:3]), .data(rom_2_data));
  ROM #(.addrWidth(24), .dataWidth(64)) rom_3 (.addr(multiplexer_1_out[26:3]), .data(rom_3_data));
  ROM #(.addrWidth(24), .dataWidth(64)) rom_4 (.addr(multiplexer_1_out[26:3]), .data(rom_4_data));
  ROM #(.addrWidth(24), .dataWidth(64)) rom_5 (.addr(multiplexer_1_out[26:3]), .data(rom_5_data));
  ROM #(.addrWidth(24), .dataWidth(64)) rom_6 (.addr(multiplexer_1_out[26:3]), .data(rom_6_data));
  ROM #(.addrWidth(24), .dataWidth(64)) rom_7 (.addr(multiplexer_1_out[26:3]), .data(rom_7_data));
  ROM #(.addrWidth(24), .dataWidth(64)) rom_8 (.addr(multiplexer_1_out[26:3]), .data(rom_8_data));
  ROM #(.addrWidth(24), .dataWidth(64)) rom_9 (.addr(multiplexer_1_out[26:3]), .data(rom_9_data));
  ROM #(.addrWidth(24), .dataWidth(64)) rom_10 (.addr(multiplexer_1_out[26:3]), .data(rom_10_data));
  ROM #(.addrWidth(24), .dataWidth(64)) rom_11 (.addr(multiplexer_1_out[26:3]), .data(rom_11_data));
  ROM #(.addrWidth(24), .dataWidth(64)) rom_12 (.addr(multiplexer_1_out[26:3]), .data(rom_12_data));
  ROM #(.addrWidth(24), .dataWidth(64)) rom_13 (.addr(multiplexer_1_out[26:3]), .data(rom_13_data));
  ROM #(.addrWidth(24), .dataWidth(64)) rom_14 (.addr(multiplexer_1_out[26:3]), .data(rom_14_data));
  ROM #(.addrWidth(24), .dataWidth(64)) rom_15 (.addr(multiplexer_1_out[26:3]), .data(rom_15_data));
  ROM #(.addrWidth(24), .dataWidth(64)) rom_16 (.addr(multiplexer_1_out[26:3]), .data(rom_16_data));
  ROM #(.addrWidth(24), .dataWidth(64)) rom_17 (.addr(multiplexer_1_out[26:3]), .data(rom_17_data));
  ROM #(.addrWidth(24), .dataWidth(64)) rom_18 (.addr(multiplexer_1_out[26:3]), .data(rom_18_data));
  ROM #(.addrWidth(24), .dataWidth(64)) rom_19 (.addr(multiplexer_1_out[26:3]), .data(rom_19_data));
  ROM #(.addrWidth(24), .dataWidth(64)) rom_20 (.addr(multiplexer_1_out[26:3]), .data(rom_20_data));
  ROM #(.addrWidth(24), .dataWidth(64)) rom_21 (.addr(multiplexer_1_out[26:3]), .data(rom_21_data));
  ROM #(.addrWidth(24), .dataWidth(64)) rom_22 (.addr(multiplexer_1_out[26:3]), .data(rom_22_data));
  ROM #(.addrWidth(24), .dataWidth(64)) rom_23 (.addr(multiplexer_1_out[26:3]), .data(rom_23_data));
  ROM #(.addrWidth(24), .dataWidth(64)) rom_24 (.addr(multiplexer_1_out[26:3]), .data(rom_24_data));
  ROM #(.addrWidth(24), .dataWidth(64)) rom_25 (.addr(multiplexer_1_out[26:3]), .data(rom_25_data));
  ROM #(.addrWidth(24), .dataWidth(64)) rom_26 (.addr(multiplexer_1_out[26:3]), .data(rom_26_data));
  ROM #(.addrWidth(24), .dataWidth(64)) rom_27 (.addr(multiplexer_1_out[26:3]), .data(rom_27_data));
  ROM #(.addrWidth(24), .dataWidth(64)) rom_28 (.addr(multiplexer_1_out[26:3]), .data(rom_28_data));
  ROM #(.addrWidth(24), .dataWidth(64)) rom_29 (.addr(multiplexer_1_out[26:3]), .data(rom_29_data));
  ROM #(.addrWidth(24), .dataWidth(64)) rom_30 (.addr(multiplexer_1_out[26:3]), .data(rom_30_data));
  ROM #(.addrWidth(24), .dataWidth(64)) rom_31 (.addr(multiplexer_1_out[26:3]), .data(rom_31_data));
  ROM #(.addrWidth(24), .dataWidth(64)) rom_32 (.addr(multiplexer_1_out[26:3]), .data(rom_32_data));
  Multiplexer #(.select(4), .width(64)) multiplexer_2 (
    .in0(rom_1_data), .in1(rom_2_data), .in2(rom_3_data), .in3(rom_4_data), .in4(rom_9_data),
    .in5(rom_10_data), .in6(rom_11_data), .in7(rom_12_data), .in8(rom_17_data), .in9(rom_18_data),
    .in10(rom_19_data), .in11(rom_20_data), .in12(rom_25_data), .in13(rom_26_data), .in14(rom_27_data),
    .in15(rom_28_data), .out(multiplexer_2_out), .sel(multiplexer_1_out[30:27]));
  Multiplexer #(.select(4), .width(64)) multiplexer_3 (
    .in0(rom_5_data), .in1(rom_6_data), .in2(rom_7_data), .in3(rom_8_data), .in4(rom_13_data),
    .in5(rom_14_data), .in6(rom_15_data), .in7(rom_16_data), .in8(rom_21_data), .in9(rom_22_data),
    .in10(rom_23_data), .in11(rom_24_data), .in12(rom_29_data), .in13(rom_30_data), .in14(rom_31_data),
    .in15(rom_32_data), .out(multiplexer_3_out), .sel(multiplexer_1_out[30:27]));
  Multiplexer #(.width(64)) multiplexer_4 (
    .in0(multiplexer_2_out), .in1(multiplexer_3_out), .out(Doubleword), .sel(multiplexer_1_out[31]));
  Multiplexer #(.width(32)) multiplexer_5 (
    .in0(Doubleword[31:0]), .in1(Doubleword[63:32]), .out(Word), .sel(subtractor_2_out[2]));
  Multiplexer #(.width(16)) multiplexer_6 (
    .in0(Word[15:0]), .in1(Word[31:16]), .out(Nibble), .sel(subtractor_2_out[1]));
  Multiplexer #(.width(8)) multiplexer_7 (.in0(Nibble[7:0]), .in1(Nibble[15:8]), .out(Byte), .sel(subtractor_2_out[0]));

  // Notes on the sheet:
  //   Tamaño de memoria accesible
  //   Longitud de byte
  //   contents of rom_1 (hex, n*v repeats v):
  //   123456789abcdef fedcba9876543210
  //   4 Gigabit
  //   4 Gigabit
  //   4 Gigabit
  //   4 Gigabit
  //   4 Gigabytes
  //   4 Giganibbles
  //   4 Giganibbles
  //   4 Gigabit
  //   4 Gigabit
  //   contents of rom_32 (hex, n*v repeats v):
  //   16777215*0 123456789abcdef
  //   4 Gigabit
  //   4 Gigabit
endmodule

module PC_Controller (
  input  [31:0] Indice_Anterior,
  input  [31:0] Indice_Salto,
  input  Tomar_Salto,
  output [31:0] Indice_Siguiente
);

  wire [31:0] adder_1_out;

  Adder #(.width(32)) adder_1 (.a(Indice_Anterior), .b(32'h4), .out(adder_1_out), .cin(1'b0));  // open: cout
  Multiplexer #(.width(32)) multiplexer_1 (
    .in0(adder_1_out), .in1(Indice_Salto), .out(Indice_Siguiente), .sel(Tomar_Salto));

  // Notes on the sheet:
  //   Alienamiento de Instrucciones
endmodule

module Instruction_Decoder (
  input  [31:0] Instruccion,
  output [6:0] Funcion_Aritmetica,
  output [4:0] Cantidad_Corrimiento,
  output [4:0] Registro_Destino,
  output [15:0] Valor_Inmediato,
  output [4:0] Registro_Objetivo,
  output [4:0] Registro_Fuente,
  output [25:0] Direccion_Inmediata,
  output Tipo_I,
  output Tipo_J,
  output Tipo_R
);

  wire comparator_1_eq, comparator_2_eq;

  Comparator #(.mode("unsigned"), .width(6)) comparator_1 (
    .a(Instruccion[31:26]), .b(6'b000011), .gt(Tipo_I), .eq(comparator_1_eq));  // open: lt
  Comparator #(.mode("unsigned"), .width(6)) comparator_2 (
    .a(6'b000010), .b(Instruccion[31:26]), .eq(comparator_2_eq));  // open: gt, lt
  Comparator #(.mode("unsigned"), .width(6)) comparator_3 (
    .a({6{1'b0}}), .b(Instruccion[31:26]), .eq(Tipo_R));  // open: gt, lt
  or or_1 (Tipo_J, comparator_1_eq, comparator_2_eq);

  assign Cantidad_Corrimiento = Instruccion[11:7];
  assign Direccion_Inmediata = Instruccion[25:0];
  assign Funcion_Aritmetica = Instruccion[6:0];
  assign Registro_Destino = Instruccion[16:12];
  assign Registro_Fuente = Instruccion[25:21];
  assign Registro_Objetivo = Instruccion[20:16];
  assign Valor_Inmediato = Instruccion[15:0];
endmodule

module Register_File_Controller (
  input  [31:0] in_1,
  input  in_2,
  input  [31:0] in_3,
  input  Reloj,
  input  Limpiar,
  input  [31:0] Entrada,
  input  [4:0] Registro_Escritura,
  input  [4:0] Registro_Lectura_A,
  input  [4:0] Registro_Lectura_B,
  output Solo_Lectura,
  output [31:0] Salida_A,
  output [31:0] Salida_B
);

  wire decoder_1_out1, decoder_1_out2, decoder_1_out3, decoder_1_out4, decoder_1_out5, decoder_1_out6,
       decoder_1_out7, decoder_1_out8, decoder_1_out9, decoder_1_out10, decoder_1_out11, decoder_1_out12,
       decoder_1_out13, decoder_1_out14, decoder_1_out15, decoder_1_out16, decoder_1_out17, decoder_1_out18,
       decoder_1_out19, decoder_1_out20, decoder_1_out21, decoder_1_out22, decoder_1_out23, decoder_1_out24,
       decoder_1_out25, decoder_1_out26, decoder_1_out27, decoder_1_out28, decoder_1_out29, decoder_1_out30,
       decoder_1_out31;
  wire [31:0] buffer_1_out, register_1_q, register_2_q, register_3_q, register_4_q, register_5_q,
       register_6_q, register_7_q, register_8_q, register_9_q, register_10_q, register_11_q, register_12_q,
       register_13_q, register_14_q, register_15_q, register_16_q, register_17_q, register_18_q,
       register_19_q, register_20_q, register_21_q, register_22_q, register_23_q, register_24_q,
       register_25_q, register_26_q, register_27_q, register_28_q, register_29_q, register_30_q,
       register_31_q, register_32_q;

  Decoder #(.enable("false"), .select(5)) decoder_1 (
    .out0(Solo_Lectura), .out1(decoder_1_out1), .out2(decoder_1_out2), .out3(decoder_1_out3),
    .out4(decoder_1_out4), .out5(decoder_1_out5), .out6(decoder_1_out6), .out7(decoder_1_out7),
    .out8(decoder_1_out8), .out9(decoder_1_out9), .out10(decoder_1_out10), .out11(decoder_1_out11),
    .out12(decoder_1_out12), .out13(decoder_1_out13), .out14(decoder_1_out14), .out15(decoder_1_out15),
    .out16(decoder_1_out16), .out17(decoder_1_out17), .out18(decoder_1_out18), .out19(decoder_1_out19),
    .out20(decoder_1_out20), .out21(decoder_1_out21), .out22(decoder_1_out22), .out23(decoder_1_out23),
    .out24(decoder_1_out24), .out25(decoder_1_out25), .out26(decoder_1_out26), .out27(decoder_1_out27),
    .out28(decoder_1_out28), .out29(decoder_1_out29), .out30(decoder_1_out30), .out31(decoder_1_out31),
    .sel(Registro_Escritura));
  Register #(.width(32)) register_1 (.D(Entrada), .en(decoder_1_out1), .clk(Reloj), .Q(register_1_q), .clr(Limpiar));
  Register #(.width(32)) register_2 (.D(Entrada), .en(decoder_1_out2), .clk(Reloj), .Q(register_2_q), .clr(Limpiar));
  Register #(.width(32)) register_3 (.D(Entrada), .en(decoder_1_out3), .clk(Reloj), .Q(register_3_q), .clr(Limpiar));
  Register #(.width(32)) register_4 (.D(Entrada), .en(decoder_1_out4), .clk(Reloj), .Q(register_4_q), .clr(Limpiar));
  Register #(.width(32)) register_5 (.D(Entrada), .en(decoder_1_out5), .clk(Reloj), .Q(register_5_q), .clr(Limpiar));
  Register #(.width(32)) register_6 (.D(Entrada), .en(decoder_1_out6), .clk(Reloj), .Q(register_6_q), .clr(Limpiar));
  Register #(.width(32)) register_7 (.D(Entrada), .en(decoder_1_out7), .clk(Reloj), .Q(register_7_q), .clr(Limpiar));
  Register #(.width(32)) register_8 (.D(Entrada), .en(decoder_1_out8), .clk(Reloj), .Q(register_8_q), .clr(Limpiar));
  Register #(.width(32)) register_9 (.D(Entrada), .en(decoder_1_out9), .clk(Reloj), .Q(register_9_q), .clr(Limpiar));
  Register #(.width(32)) register_10 (.D(Entrada), .en(decoder_1_out10), .clk(Reloj), .Q(register_10_q), .clr(Limpiar));
  Register #(.width(32)) register_11 (.D(Entrada), .en(decoder_1_out11), .clk(Reloj), .Q(register_11_q), .clr(Limpiar));
  Register #(.width(32)) register_12 (.D(Entrada), .en(decoder_1_out12), .clk(Reloj), .Q(register_12_q), .clr(Limpiar));
  Register #(.width(32)) register_13 (.D(Entrada), .en(decoder_1_out13), .clk(Reloj), .Q(register_13_q), .clr(Limpiar));
  Register #(.width(32)) register_14 (.D(Entrada), .en(decoder_1_out14), .clk(Reloj), .Q(register_14_q), .clr(Limpiar));
  Register #(.width(32)) register_15 (.D(Entrada), .en(decoder_1_out15), .clk(Reloj), .Q(register_15_q), .clr(Limpiar));
  Register #(.width(32)) register_16 (.D(Entrada), .en(decoder_1_out16), .clk(Reloj), .Q(register_16_q), .clr(Limpiar));
  Register #(.width(32)) register_17 (.D(Entrada), .en(decoder_1_out17), .clk(Reloj), .Q(register_17_q), .clr(Limpiar));
  Register #(.width(32)) register_18 (.D(Entrada), .en(decoder_1_out18), .clk(Reloj), .Q(register_18_q), .clr(Limpiar));
  Register #(.width(32)) register_19 (.D(Entrada), .en(decoder_1_out19), .clk(Reloj), .Q(register_19_q), .clr(Limpiar));
  Register #(.width(32)) register_20 (.D(Entrada), .en(decoder_1_out20), .clk(Reloj), .Q(register_20_q), .clr(Limpiar));
  Register #(.width(32)) register_21 (.D(Entrada), .en(decoder_1_out21), .clk(Reloj), .Q(register_21_q), .clr(Limpiar));
  Register #(.width(32)) register_22 (.D(Entrada), .en(decoder_1_out22), .clk(Reloj), .Q(register_22_q), .clr(Limpiar));
  Register #(.width(32)) register_23 (.D(Entrada), .en(decoder_1_out23), .clk(Reloj), .Q(register_23_q), .clr(Limpiar));
  Register #(.width(32)) register_24 (.D(Entrada), .en(decoder_1_out24), .clk(Reloj), .Q(register_24_q), .clr(Limpiar));
  Register #(.width(32)) register_25 (.D(Entrada), .en(decoder_1_out25), .clk(Reloj), .Q(register_25_q), .clr(Limpiar));
  Register #(.width(32)) register_26 (.D(Entrada), .en(decoder_1_out26), .clk(Reloj), .Q(register_26_q), .clr(Limpiar));
  Register #(.width(32)) register_27 (.D(Entrada), .en(decoder_1_out27), .clk(Reloj), .Q(register_27_q), .clr(Limpiar));
  Register #(.width(32)) register_28 (.D(Entrada), .en(decoder_1_out28), .clk(Reloj), .Q(register_28_q), .clr(Limpiar));
  Register #(.width(32)) register_29 (.D(Entrada), .en(decoder_1_out29), .clk(Reloj), .Q(register_29_q), .clr(Limpiar));
  Register #(.width(32)) register_30 (.D(Entrada), .en(decoder_1_out30), .clk(Reloj), .Q(register_30_q), .clr(Limpiar));
  Register #(.width(32)) register_31 (.D(Entrada), .en(decoder_1_out31), .clk(Reloj), .Q(register_31_q), .clr(Limpiar));
  Register #(.width(32)) register_32 (.D(in_1), .en(in_2), .clk(in_2), .Q(register_32_q));  // open: clr
  assign buffer_1_out = register_32_q;  // Buffer buffer_1, 32 bits wide
  assign buffer_1_out = in_3;  // Buffer buffer_2, 32 bits wide
  Multiplexer #(.select(5), .width(32)) multiplexer_1 (
    .in0({32{1'b0}}), .in1(register_1_q), .in2(register_2_q), .in3(register_3_q), .in4(register_4_q),
    .in5(register_5_q), .in6(register_6_q), .in7(register_7_q), .in8(register_8_q), .in9(register_9_q),
    .in10(register_10_q), .in11(register_11_q), .in12(register_12_q), .in13(register_13_q),
    .in14(register_14_q), .in15(register_15_q), .in16(register_16_q), .in17(register_17_q),
    .in18(register_18_q), .in19(register_19_q), .in20(register_20_q), .in21(register_21_q),
    .in22(register_22_q), .in23(register_23_q), .in24(register_24_q), .in25(register_25_q),
    .in26(register_26_q), .in27(register_27_q), .in28(register_28_q), .in29(register_29_q),
    .in30(register_30_q), .in31(register_31_q), .out(Salida_A), .sel(Registro_Lectura_A));
  Multiplexer #(.select(5), .width(32)) multiplexer_2 (
    .in0({32{1'b0}}), .in1(register_1_q), .in2(register_2_q), .in3(register_3_q), .in4(register_4_q),
    .in5(register_5_q), .in6(register_6_q), .in7(register_7_q), .in8(register_8_q), .in9(register_9_q),
    .in10(register_10_q), .in11(register_11_q), .in12(register_12_q), .in13(register_13_q),
    .in14(register_14_q), .in15(register_15_q), .in16(register_16_q), .in17(register_17_q),
    .in18(register_18_q), .in19(register_19_q), .in20(register_20_q), .in21(register_21_q),
    .in22(register_22_q), .in23(register_23_q), .in24(register_24_q), .in25(register_25_q),
    .in26(register_26_q), .in27(register_27_q), .in28(register_28_q), .in29(register_29_q),
    .in30(register_30_q), .in31(register_31_q), .out(Salida_B), .sel(Registro_Lectura_B));

  // Other names for the same wires on the sheet: Direccion_Escritura[4:0] = Registro_Escritura;
  //   Direccion_Lectura_A[4:0] = Registro_Lectura_A; Direccion_Lectura_B[4:0] = Registro_Lectura_B
endmodule

module Four_GB_RAM_Controller (
  input  Reloj,
  input  Limpiar,
  input  Bloquear,
  input  Escribir,
  input  [31:0] Direccion_32_bits,
  input  Usar_Litte_Endian,
  input  [31:0] Entrada,
  output [63:0] Doubleword,
  output [31:0] Word,
  output [15:0] Nibble,
  output [7:0] Byte
);

  wire and_1_out, and_2_out, and_3_out, and_4_out, and_5_out, and_6_out, and_7_out, and_8_out, and_9_out,
       and_10_out, and_11_out, and_12_out, and_13_out, and_14_out, and_15_out, and_16_out, and_17_out,
       and_18_out, and_19_out, and_20_out, and_21_out, and_22_out, and_23_out, and_24_out, and_25_out,
       and_26_out, and_27_out, and_28_out, and_30_out, and_31_out, and_32_out, and_33_out, and_34_out,
       and_35_out, and_36_out, and_37_out, and_38_out, and_39_out, and_40_out, and_41_out, and_42_out,
       and_43_out, and_44_out, and_45_out, and_46_out, and_47_out, and_48_out, and_49_out, and_50_out,
       and_51_out, and_52_out, and_53_out, and_54_out, and_55_out, and_56_out, and_57_out, and_58_out,
       and_59_out, and_60_out, and_61_out, and_62_out, and_63_out, and_64_out, and_65_out, and_66_out,
       and_67_out, and_68_out, and_69_out, and_70_out, and_71_out, and_72_out, and_73_out, and_74_out,
       and_75_out, and_76_out, and_77_out, and_78_out, and_79_out, and_80_out, and_81_out, and_82_out,
       and_83_out, and_84_out, and_85_out, and_86_out, and_87_out, and_88_out, and_89_out, and_90_out,
       and_91_out, and_92_out, and_93_out, and_94_out, and_95_out, and_96_out, and_97_out, and_98_out,
       and_99_out, and_100_out, and_101_out, and_102_out, and_103_out, decoder_1_out0, decoder_1_out1,
       decoder_2_out0, decoder_2_out1, decoder_2_out2, decoder_2_out3, decoder_3_out0, decoder_3_out1,
       decoder_3_out2, decoder_3_out3, decoder_4_out0, decoder_4_out1, decoder_4_out2, decoder_4_out3,
       decoder_5_out0, decoder_5_out1, decoder_5_out2, decoder_5_out3, not_1_out;
  wire [1:0] multiplexer_1_out_3, multiplexer_1_out_4;
  wire [2:0] subtractor_2_out;
  wire [23:0] multiplexer_1_out_2;
  wire [31:0] multiplexer_1_out, subtractor_1_out;
  wire [63:0] and_29_out, bit_extender_1_out, bit_extender_2_out, controlled_buffer_1_out,
       controlled_buffer_18_out, multiplexer_5_out, or_1_out, ram_1_dout, ram_2_dout, ram_3_dout, ram_4_dout,
       ram_5_dout, ram_6_dout, ram_7_dout, ram_8_dout, ram_9_dout, ram_10_dout, ram_11_dout, ram_12_dout,
       ram_13_dout, ram_14_dout, ram_15_dout, ram_16_dout, ram_17_dout, ram_18_dout, ram_19_dout,
       ram_20_dout, ram_21_dout, ram_22_dout, ram_23_dout, ram_24_dout, ram_25_dout, ram_26_dout,
       ram_27_dout, ram_28_dout, ram_29_dout, ram_30_dout, ram_31_dout, ram_32_dout, shifter_1_out, xor_1_out;

  Subtractor #(.width(32)) subtractor_1 (
    .a({32{1'b1}}), .b(Direccion_32_bits), .out(subtractor_1_out), .bin(1'b0));  // open: bout
  Multiplexer #(.width(32)) multiplexer_1 (
    .in0(Direccion_32_bits), .in1(subtractor_1_out),
    .out({multiplexer_1_out[31], multiplexer_1_out_4, multiplexer_1_out_3, multiplexer_1_out_2, multiplexer_1_out[2:0]}),
    .sel(Usar_Litte_Endian));
  Subtractor #(.width(3)) subtractor_2 (
    .a(3'b111), .b(multiplexer_1_out[2:0]), .out(subtractor_2_out), .bin(1'b0));  // open: bout
  // Probe on subtractor_2_out
  and and_1 (and_1_out, ~Escribir, ~Bloquear);  // AND_Gate
  and and_2 (and_2_out, Escribir, ~Bloquear);  // AND_Gate
  Decoder #(.enable("false")) decoder_1 (.out0(decoder_1_out0), .out1(decoder_1_out1), .sel(multiplexer_1_out[31]));
  // Probe on multiplexer_1_out_2
  // Probe on multiplexer_1_out_4
  // Probe on multiplexer_1_out_3
  and and_3 (and_3_out, decoder_1_out0, and_2_out);
  and and_4 (and_4_out, decoder_1_out0, and_1_out);
  // Probe on {multiplexer_1_out_4, multiplexer_1_out_3, multiplexer_1_out_2}
  Decoder #(.enable("false"), .select(2)) decoder_2 (
    .out0(decoder_2_out0), .out1(decoder_2_out1), .out2(decoder_2_out2), .out3(decoder_2_out3),
    .sel(multiplexer_1_out_4));
  Decoder #(.enable("false"), .select(2)) decoder_3 (
    .out0(decoder_3_out0), .out1(decoder_3_out1), .out2(decoder_3_out2), .out3(decoder_3_out3),
    .sel(multiplexer_1_out_3));
  and and_5 (and_5_out, decoder_3_out0, decoder_2_out0);
  and and_6 (and_6_out, and_5_out, and_3_out);
  and and_7 (and_7_out, and_5_out, and_4_out);
  and and_8 (and_8_out, decoder_3_out0, decoder_2_out1);
  and and_9 (and_9_out, and_8_out, and_3_out);
  and and_10 (and_10_out, and_8_out, and_4_out);
  and and_11 (and_11_out, decoder_3_out0, decoder_2_out2);
  and and_12 (and_12_out, and_11_out, and_3_out);
  and and_13 (and_13_out, and_11_out, and_4_out);
  and and_14 (and_14_out, decoder_3_out0, decoder_2_out3);
  and and_15 (and_15_out, and_14_out, and_3_out);
  and and_16 (and_16_out, and_14_out, and_4_out);
  RAM #(.addrWidth(24), .clearpin("true"), .dataWidth(64)) ram_1 (
    .addr(multiplexer_1_out_2), .we(and_6_out), .oe(and_7_out), .clk(Reloj), .din(or_1_out),
    .dout(ram_1_dout), .clr(Limpiar));
  RAM #(.addrWidth(24), .clearpin("true"), .dataWidth(64)) ram_2 (
    .addr(multiplexer_1_out_2), .we(and_9_out), .oe(and_10_out), .clk(Reloj), .din(or_1_out),
    .dout(ram_2_dout), .clr(Limpiar));
  RAM #(.addrWidth(24), .clearpin("true"), .dataWidth(64)) ram_3 (
    .addr(multiplexer_1_out_2), .we(and_12_out), .oe(and_13_out), .clk(Reloj), .din(or_1_out),
    .dout(ram_3_dout), .clr(Limpiar));
  RAM #(.addrWidth(24), .clearpin("true"), .dataWidth(64)) ram_4 (
    .addr(multiplexer_1_out_2), .we(and_15_out), .oe(and_16_out), .clk(Reloj), .din(or_1_out),
    .dout(ram_4_dout), .clr(Limpiar));
  assign controlled_buffer_1_out = and_5_out ? ram_1_dout : 64'bz;  // Controlled_Buffer controlled_buffer_1
  assign controlled_buffer_1_out = and_8_out ? ram_2_dout : 64'bz;  // Controlled_Buffer controlled_buffer_2
  assign controlled_buffer_1_out = and_11_out ? ram_3_dout : 64'bz;  // Controlled_Buffer controlled_buffer_3
  assign controlled_buffer_1_out = and_14_out ? ram_4_dout : 64'bz;  // Controlled_Buffer controlled_buffer_4
  assign Doubleword = decoder_1_out0 ? controlled_buffer_1_out : 64'bz;  // Controlled_Buffer controlled_buffer_5
  and and_17 (and_17_out, decoder_3_out1, decoder_2_out0);
  and and_18 (and_18_out, decoder_3_out1, decoder_2_out1);
  and and_19 (and_19_out, decoder_3_out1, decoder_2_out2);
  and and_20 (and_20_out, decoder_3_out1, decoder_2_out3);
  Multiplexer #(.width(32)) multiplexer_2 (
    .in0(Doubleword[31:0]), .in1(Doubleword[63:32]), .out(Word), .sel(subtractor_2_out[2]));
  not not_1 (not_1_out, subtractor_2_out[2]);
  and and_21 (and_21_out, and_17_out, and_3_out);
  and and_22 (and_22_out, and_17_out, and_4_out);
  and and_23 (and_23_out, and_18_out, and_3_out);
  and and_24 (and_24_out, and_18_out, and_4_out);
  and and_25 (and_25_out, and_19_out, and_3_out);
  and and_26 (and_26_out, and_19_out, and_4_out);
  and and_27 (and_27_out, and_20_out, and_3_out);
  and and_28 (and_28_out, and_20_out, and_4_out);
  Multiplexer #(.width(16)) multiplexer_3 (
    .in0(Word[15:0]), .in1(Word[31:16]), .out(Nibble), .sel(subtractor_2_out[1]));
  Multiplexer #(.width(8)) multiplexer_4 (.in0(Nibble[7:0]), .in1(Nibble[15:8]), .out(Byte), .sel(subtractor_2_out[0]));
  assign bit_extender_1_out = {{63{not_1_out}}, not_1_out};  // Bit_Extender bit_extender_1
  assign bit_extender_2_out = {{32{1'b0}}, Entrada};  // Bit_Extender bit_extender_2
  RAM #(.addrWidth(24), .clearpin("true"), .dataWidth(64)) ram_5 (
    .addr(multiplexer_1_out_2), .we(and_21_out), .oe(and_22_out), .clk(Reloj), .din(or_1_out),
    .dout(ram_5_dout), .clr(Limpiar));
  RAM #(.addrWidth(24), .clearpin("true"), .dataWidth(64)) ram_6 (
    .addr(multiplexer_1_out_2), .we(and_23_out), .oe(and_24_out), .clk(Reloj), .din(or_1_out),
    .dout(ram_6_dout), .clr(Limpiar));
  RAM #(.addrWidth(24), .clearpin("true"), .dataWidth(64)) ram_7 (
    .addr(multiplexer_1_out_2), .we(and_25_out), .oe(and_26_out), .clk(Reloj), .din(or_1_out),
    .dout(ram_7_dout), .clr(Limpiar));
  RAM #(.addrWidth(24), .clearpin("true"), .dataWidth(64)) ram_8 (
    .addr(multiplexer_1_out_2), .we(and_27_out), .oe(and_28_out), .clk(Reloj), .din(or_1_out),
    .dout(ram_8_dout), .clr(Limpiar));
  assign xor_1_out = 64'hffffffff ^ bit_extender_1_out;  // XOR_Gate xor_1, 64 bits wide
  Multiplexer #(.width(64)) multiplexer_5 (
    .in0(bit_extender_2_out), .in1(shifter_1_out), .out(multiplexer_5_out), .sel(subtractor_2_out[2]));
  Shifter #(.width(64)) shifter_1 (.in(bit_extender_2_out), .\dist (6'b100000), .out(shifter_1_out));
  assign and_29_out = Doubleword & xor_1_out;  // AND_Gate and_29, 64 bits wide
  assign or_1_out = and_29_out | multiplexer_5_out;  // OR_Gate or_1, 64 bits wide
  assign controlled_buffer_1_out = and_17_out ? ram_5_dout : 64'bz;  // Controlled_Buffer controlled_buffer_6
  assign controlled_buffer_1_out = and_18_out ? ram_6_dout : 64'bz;  // Controlled_Buffer controlled_buffer_7
  assign controlled_buffer_1_out = and_19_out ? ram_7_dout : 64'bz;  // Controlled_Buffer controlled_buffer_8
  assign controlled_buffer_1_out = and_20_out ? ram_8_dout : 64'bz;  // Controlled_Buffer controlled_buffer_9
  // Probe on or_1_out
  and and_30 (and_30_out, decoder_3_out2, decoder_2_out0);
  and and_31 (and_31_out, decoder_3_out2, decoder_2_out1);
  and and_32 (and_32_out, decoder_3_out2, decoder_2_out2);
  and and_33 (and_33_out, decoder_3_out2, decoder_2_out3);
  RAM #(.addrWidth(24), .clearpin("true"), .dataWidth(64)) ram_9 (
    .addr(multiplexer_1_out_2), .we(and_34_out), .oe(and_35_out), .clk(Reloj), .din(or_1_out),
    .dout(ram_9_dout), .clr(Limpiar));
  and and_34 (and_34_out, and_30_out, and_3_out);
  and and_35 (and_35_out, and_30_out, and_4_out);
  RAM #(.addrWidth(24), .clearpin("true"), .dataWidth(64)) ram_10 (
    .addr(multiplexer_1_out_2), .we(and_36_out), .oe(and_37_out), .clk(Reloj), .din(or_1_out),
    .dout(ram_10_dout), .clr(Limpiar));
  and and_36 (and_36_out, and_31_out, and_3_out);
  and and_37 (and_37_out, and_31_out, and_4_out);
  RAM #(.addrWidth(24), .clearpin("true"), .dataWidth(64)) ram_11 (
    .addr(multiplexer_1_out_2), .we(and_38_out), .oe(and_39_out), .clk(Reloj), .din(or_1_out),
    .dout(ram_11_dout), .clr(Limpiar));
  and and_38 (and_38_out, and_32_out, and_3_out);
  and and_39 (and_39_out, and_32_out, and_4_out);
  RAM #(.addrWidth(24), .clearpin("true"), .dataWidth(64)) ram_12 (
    .addr(multiplexer_1_out_2), .we(and_40_out), .oe(and_41_out), .clk(Reloj), .din(or_1_out),
    .dout(ram_12_dout), .clr(Limpiar));
  and and_40 (and_40_out, and_33_out, and_3_out);
  and and_41 (and_41_out, and_33_out, and_4_out);
  and and_42 (and_42_out, decoder_3_out3, decoder_2_out0);
  assign controlled_buffer_1_out = and_30_out ? ram_9_dout : 64'bz;  // Controlled_Buffer controlled_buffer_10
  and and_43 (and_43_out, decoder_3_out3, decoder_2_out1);
  assign controlled_buffer_1_out = and_31_out ? ram_10_dout : 64'bz;  // Controlled_Buffer controlled_buffer_11
  and and_44 (and_44_out, decoder_3_out3, decoder_2_out2);
  assign controlled_buffer_1_out = and_32_out ? ram_11_dout : 64'bz;  // Controlled_Buffer controlled_buffer_12
  and and_45 (and_45_out, decoder_3_out3, decoder_2_out3);
  assign controlled_buffer_1_out = and_33_out ? ram_12_dout : 64'bz;  // Controlled_Buffer controlled_buffer_13
  and and_46 (and_46_out, and_42_out, and_3_out);
  and and_47 (and_47_out, and_42_out, and_4_out);
  and and_48 (and_48_out, and_43_out, and_3_out);
  and and_49 (and_49_out, and_43_out, and_4_out);
  and and_50 (and_50_out, and_44_out, and_3_out);
  and and_51 (and_51_out, and_44_out, and_4_out);
  and and_52 (and_52_out, and_45_out, and_3_out);
  and and_53 (and_53_out, and_45_out, and_4_out);
  RAM #(.addrWidth(24), .clearpin("true"), .dataWidth(64)) ram_13 (
    .addr(multiplexer_1_out_2), .we(and_46_out), .oe(and_47_out), .clk(Reloj), .din(or_1_out),
    .dout(ram_13_dout), .clr(Limpiar));
  RAM #(.addrWidth(24), .clearpin("true"), .dataWidth(64)) ram_14 (
    .addr(multiplexer_1_out_2), .we(and_48_out), .oe(and_49_out), .clk(Reloj), .din(or_1_out),
    .dout(ram_14_dout), .clr(Limpiar));
  RAM #(.addrWidth(24), .clearpin("true"), .dataWidth(64)) ram_15 (
    .addr(multiplexer_1_out_2), .we(and_50_out), .oe(and_51_out), .clk(Reloj), .din(or_1_out),
    .dout(ram_15_dout), .clr(Limpiar));
  RAM #(.addrWidth(24), .clearpin("true"), .dataWidth(64)) ram_16 (
    .addr(multiplexer_1_out_2), .we(and_52_out), .oe(and_53_out), .clk(Reloj), .din(or_1_out),
    .dout(ram_16_dout), .clr(Limpiar));
  assign controlled_buffer_1_out = and_42_out ? ram_13_dout : 64'bz;  // Controlled_Buffer controlled_buffer_14
  assign controlled_buffer_1_out = and_43_out ? ram_14_dout : 64'bz;  // Controlled_Buffer controlled_buffer_15
  assign controlled_buffer_1_out = and_44_out ? ram_15_dout : 64'bz;  // Controlled_Buffer controlled_buffer_16
  assign controlled_buffer_1_out = and_45_out ? ram_16_dout : 64'bz;  // Controlled_Buffer controlled_buffer_17
  and and_54 (and_54_out, decoder_1_out1, and_2_out);
  and and_55 (and_55_out, decoder_1_out1, and_1_out);
  Decoder #(.enable("false"), .select(2)) decoder_4 (
    .out0(decoder_4_out0), .out1(decoder_4_out1), .out2(decoder_4_out2), .out3(decoder_4_out3),
    .sel(multiplexer_1_out_4));
  Decoder #(.enable("false"), .select(2)) decoder_5 (
    .out0(decoder_5_out0), .out1(decoder_5_out1), .out2(decoder_5_out2), .out3(decoder_5_out3),
    .sel(multiplexer_1_out_3));
  and and_56 (and_56_out, decoder_5_out0, decoder_4_out0);
  and and_57 (and_57_out, and_56_out, and_54_out);
  and and_58 (and_58_out, and_56_out, and_55_out);
  and and_59 (and_59_out, decoder_5_out0, decoder_4_out1);
  and and_60 (and_60_out, and_59_out, and_54_out);
  and and_61 (and_61_out, and_59_out, and_55_out);
  and and_62 (and_62_out, decoder_5_out0, decoder_4_out2);
  and and_63 (and_63_out, and_62_out, and_54_out);
  and and_64 (and_64_out, and_62_out, and_55_out);
  and and_65 (and_65_out, decoder_5_out0, decoder_4_out3);
  and and_66 (and_66_out, and_65_out, and_54_out);
  and and_67 (and_67_out, and_65_out, and_55_out);
  RAM #(.addrWidth(24), .clearpin("true"), .dataWidth(64)) ram_17 (
    .addr(multiplexer_1_out_2), .we(and_57_out), .oe(and_58_out), .clk(Reloj), .din(or_1_out),
    .dout(ram_17_dout), .clr(Limpiar));
  RAM #(.addrWidth(24), .clearpin("true"), .dataWidth(64)) ram_18 (
    .addr(multiplexer_1_out_2), .we(and_60_out), .oe(and_61_out), .clk(Reloj), .din(or_1_out),
    .dout(ram_18_dout), .clr(Limpiar));
  RAM #(.addrWidth(24), .clearpin("true"), .dataWidth(64)) ram_19 (
    .addr(multiplexer_1_out_2), .we(and_63_out), .oe(and_64_out), .clk(Reloj), .din(or_1_out),
    .dout(ram_19_dout), .clr(Limpiar));
  RAM #(.addrWidth(24), .clearpin("true"), .dataWidth(64)) ram_20 (
    .addr(multiplexer_1_out_2), .we(and_66_out), .oe(and_67_out), .clk(Reloj), .din(or_1_out),
    .dout(ram_20_dout), .clr(Limpiar));
  assign controlled_buffer_18_out = and_56_out ? ram_17_dout : 64'bz;  // Controlled_Buffer controlled_buffer_18
  assign controlled_buffer_18_out = and_59_out ? ram_18_dout : 64'bz;  // Controlled_Buffer controlled_buffer_19
  assign controlled_buffer_18_out = and_62_out ? ram_19_dout : 64'bz;  // Controlled_Buffer controlled_buffer_20
  assign controlled_buffer_18_out = and_65_out ? ram_20_dout : 64'bz;  // Controlled_Buffer controlled_buffer_21
  assign Doubleword = decoder_1_out1 ? controlled_buffer_18_out : 64'bz;  // Controlled_Buffer controlled_buffer_22
  and and_68 (and_68_out, decoder_5_out1, decoder_4_out0);
  and and_69 (and_69_out, decoder_5_out1, decoder_4_out1);
  and and_70 (and_70_out, decoder_5_out1, decoder_4_out2);
  and and_71 (and_71_out, decoder_5_out1, decoder_4_out3);
  and and_72 (and_72_out, and_68_out, and_54_out);
  and and_73 (and_73_out, and_68_out, and_55_out);
  and and_74 (and_74_out, and_69_out, and_54_out);
  and and_75 (and_75_out, and_69_out, and_55_out);
  and and_76 (and_76_out, and_70_out, and_54_out);
  and and_77 (and_77_out, and_70_out, and_55_out);
  and and_78 (and_78_out, and_71_out, and_54_out);
  and and_79 (and_79_out, and_71_out, and_55_out);
  RAM #(.addrWidth(24), .clearpin("true"), .dataWidth(64)) ram_21 (
    .addr(multiplexer_1_out_2), .we(and_72_out), .oe(and_73_out), .clk(Reloj), .din(or_1_out),
    .dout(ram_21_dout), .clr(Limpiar));
  RAM #(.addrWidth(24), .clearpin("true"), .dataWidth(64)) ram_22 (
    .addr(multiplexer_1_out_2), .we(and_74_out), .oe(and_75_out), .clk(Reloj), .din(or_1_out),
    .dout(ram_22_dout), .clr(Limpiar));
  RAM #(.addrWidth(24), .clearpin("true"), .dataWidth(64)) ram_23 (
    .addr(multiplexer_1_out_2), .we(and_76_out), .oe(and_77_out), .clk(Reloj), .din(or_1_out),
    .dout(ram_23_dout), .clr(Limpiar));
  RAM #(.addrWidth(24), .clearpin("true"), .dataWidth(64)) ram_24 (
    .addr(multiplexer_1_out_2), .we(and_78_out), .oe(and_79_out), .clk(Reloj), .din(or_1_out),
    .dout(ram_24_dout), .clr(Limpiar));
  assign controlled_buffer_18_out = and_68_out ? ram_21_dout : 64'bz;  // Controlled_Buffer controlled_buffer_23
  assign controlled_buffer_18_out = and_69_out ? ram_22_dout : 64'bz;  // Controlled_Buffer controlled_buffer_24
  assign controlled_buffer_18_out = and_70_out ? ram_23_dout : 64'bz;  // Controlled_Buffer controlled_buffer_25
  assign controlled_buffer_18_out = and_71_out ? ram_24_dout : 64'bz;  // Controlled_Buffer controlled_buffer_26
  and and_80 (and_80_out, decoder_5_out2, decoder_4_out0);
  and and_81 (and_81_out, decoder_5_out2, decoder_4_out1);
  and and_82 (and_82_out, decoder_5_out2, decoder_4_out2);
  and and_83 (and_83_out, decoder_5_out2, decoder_4_out3);
  RAM #(.addrWidth(24), .clearpin("true"), .dataWidth(64)) ram_25 (
    .addr(multiplexer_1_out_2), .we(and_84_out), .oe(and_85_out), .clk(Reloj), .din(or_1_out),
    .dout(ram_25_dout), .clr(Limpiar));
  and and_84 (and_84_out, and_80_out, and_54_out);
  and and_85 (and_85_out, and_80_out, and_55_out);
  RAM #(.addrWidth(24), .clearpin("true"), .dataWidth(64)) ram_26 (
    .addr(multiplexer_1_out_2), .we(and_86_out), .oe(and_87_out), .clk(Reloj), .din(or_1_out),
    .dout(ram_26_dout), .clr(Limpiar));
  and and_86 (and_86_out, and_81_out, and_54_out);
  and and_87 (and_87_out, and_81_out, and_55_out);
  RAM #(.addrWidth(24), .clearpin("true"), .dataWidth(64)) ram_27 (
    .addr(multiplexer_1_out_2), .we(and_88_out), .oe(and_89_out), .clk(Reloj), .din(or_1_out),
    .dout(ram_27_dout), .clr(Limpiar));
  and and_88 (and_88_out, and_82_out, and_54_out);
  and and_89 (and_89_out, and_82_out, and_55_out);
  RAM #(.addrWidth(24), .clearpin("true"), .dataWidth(64)) ram_28 (
    .addr(multiplexer_1_out_2), .we(and_90_out), .oe(and_91_out), .clk(Reloj), .din(or_1_out),
    .dout(ram_28_dout), .clr(Limpiar));
  and and_90 (and_90_out, and_83_out, and_54_out);
  and and_91 (and_91_out, and_83_out, and_55_out);
  and and_92 (and_92_out, decoder_5_out3, decoder_4_out0);
  assign controlled_buffer_18_out = and_80_out ? ram_25_dout : 64'bz;  // Controlled_Buffer controlled_buffer_27
  and and_93 (and_93_out, decoder_5_out3, decoder_4_out1);
  assign controlled_buffer_18_out = and_81_out ? ram_26_dout : 64'bz;  // Controlled_Buffer controlled_buffer_28
  and and_94 (and_94_out, decoder_5_out3, decoder_4_out2);
  assign controlled_buffer_18_out = and_82_out ? ram_27_dout : 64'bz;  // Controlled_Buffer controlled_buffer_29
  and and_95 (and_95_out, decoder_5_out3, decoder_4_out3);
  assign controlled_buffer_18_out = and_83_out ? ram_28_dout : 64'bz;  // Controlled_Buffer controlled_buffer_30
  and and_96 (and_96_out, and_92_out, and_54_out);
  and and_97 (and_97_out, and_92_out, and_55_out);
  and and_98 (and_98_out, and_93_out, and_54_out);
  and and_99 (and_99_out, and_93_out, and_55_out);
  and and_100 (and_100_out, and_94_out, and_54_out);
  and and_101 (and_101_out, and_94_out, and_55_out);
  and and_102 (and_102_out, and_95_out, and_54_out);
  and and_103 (and_103_out, and_95_out, and_55_out);
  RAM #(.addrWidth(24), .clearpin("true"), .dataWidth(64)) ram_29 (
    .addr(multiplexer_1_out_2), .we(and_96_out), .oe(and_97_out), .clk(Reloj), .din(or_1_out),
    .dout(ram_29_dout), .clr(Limpiar));
  RAM #(.addrWidth(24), .clearpin("true"), .dataWidth(64)) ram_30 (
    .addr(multiplexer_1_out_2), .we(and_98_out), .oe(and_99_out), .clk(Reloj), .din(or_1_out),
    .dout(ram_30_dout), .clr(Limpiar));
  RAM #(.addrWidth(24), .clearpin("true"), .dataWidth(64)) ram_31 (
    .addr(multiplexer_1_out_2), .we(and_100_out), .oe(and_101_out), .clk(Reloj), .din(or_1_out),
    .dout(ram_31_dout), .clr(Limpiar));
  RAM #(.addrWidth(24), .clearpin("true"), .dataWidth(64)) ram_32 (
    .addr(multiplexer_1_out_2), .we(and_102_out), .oe(and_103_out), .clk(Reloj), .din(or_1_out),
    .dout(ram_32_dout), .clr(Limpiar));
  assign controlled_buffer_18_out = and_92_out ? ram_29_dout : 64'bz;  // Controlled_Buffer controlled_buffer_31
  assign controlled_buffer_18_out = and_93_out ? ram_30_dout : 64'bz;  // Controlled_Buffer controlled_buffer_32
  assign controlled_buffer_18_out = and_94_out ? ram_31_dout : 64'bz;  // Controlled_Buffer controlled_buffer_33
  assign controlled_buffer_18_out = and_95_out ? ram_32_dout : 64'bz;  // Controlled_Buffer controlled_buffer_34

  // Notes on the sheet:
  //   Tamaño de memoria accesible
  //   Longitud de byte
  //   (Little Endian)
  //   (Big Endian)
  //   2 Gigabytes
  //   2 Gigabytes
endmodule

module Thirty_Two_Bit_RAM_Contender (
  input  Reiniciar,
  input  Reloj,
  input  Solicitar_A,
  input  Escribir_A,
  input  [31:0] Direccion_A,
  input  [31:0] Entrada_A,
  input  Solicitar_B,
  input  Escribir_B,
  input  [31:0] Direccion_B,
  input  [31:0] Entrada_B,
  output Atendiendo_B,
  output Escribir,
  output [31:0] Direccion,
  output [31:0] Entrada
);

  wire random_1_out;
  wire [1:0] bit_extender_1_out, bit_extender_2_out, Solicitantes;

  assign bit_extender_1_out = {{1{1'b0}}, Solicitar_A};  // Bit_Extender bit_extender_1
  assign bit_extender_2_out = {{1{1'b0}}, Solicitar_B};  // Bit_Extender bit_extender_2
  Random #(.width(1)) random_1 (.clr(Reiniciar), .next(1'b1), .clk(Reloj), .out(random_1_out));
  Adder #(.width(2)) adder_1 (.a(bit_extender_1_out), .b(bit_extender_2_out), .out(Solicitantes));  // open: cin, cout
  Multiplexer multiplexer_1 (.in0(Escribir_A), .in1(Escribir_B), .out(Escribir), .sel(Atendiendo_B));
  Multiplexer #(.width(32)) multiplexer_2 (.in0(Direccion_A), .in1(Direccion_B), .out(Direccion), .sel(Atendiendo_B));
  Multiplexer #(.width(32)) multiplexer_3 (.in0(Entrada_A), .in1(Entrada_B), .out(Entrada), .sel(Atendiendo_B));
  Multiplexer #(.select(2)) multiplexer_4 (
    .in0(random_1_out), .in1(Solicitar_B), .in2(random_1_out), .in3(random_1_out), .out(Atendiendo_B),
    .sel(Solicitantes));

  // Other names for the same wires on the sheet: Solicitante_Atendido = Atendiendo_B
endmodule

module MIPS_ALU (
  input  Tipo_J,
  input  Tipo_I,
  input  Tipo_R,
  input  [6:0] Funcion_Aritmetica,
  input  [4:0] Cantidad_Corrimiento,
  input  [31:0] Contenido_Registro_Fuente,
  input  [31:0] Contenido_Registro_Objetivo,
  input  [15:0] Valor_Inmediato,
  input  [25:0] Direccion_Inmediata,
  input  [31:0] Indice_PC
);

  wire adder_4_cout, adder_5_cout, bitfinder_1_index, comparator_1_eq, comparator_1_gt, comparator_2_eq,
       comparator_2_gt, comparator_4_eq, Origen_Es_Igual, Origen_Es_Mayor, Origen_Es_Mayor_U,
       Origen_Es_Menor, Origen_Es_Menor_I, Origen_Es_Menor_I_U, Origen_Es_Menor_U, Overflow_ADD,
       Overflow_ADD_I, Overflow_Direccion_Previo_Salto, Overflow_Salto_Condicional, Overflow_Salto_J_JAL,
       Overflow_SUB, Salto_Desalineado;
  wire [1:0] bit_extender_8_out;
  wire [4:0] bit_extender_2_out, bit_extender_4_out, bit_extender_5_out;
  wire [15:0] multiplier_3_cout, multiplier_3_out;
  wire [27:0] bit_extender_1_out, shifter_1_out;
  wire [31:0] adder_1_out, adder_4_out, and_3_out, bit_extender_3_out, Cociente_DIV, Cociente_DIV_U,
       Direccion_Previo_Salto, Direccion_Salto, Direccion_Salto_Condicional, Direccion_Salto_J_JAL,
       Inmediato_Extendido, Inmediato_Extendido_U, Parte_Inferior_MULT, Parte_Inferior_MULT_U,
       Parte_Superior_MULT, Parte_Superior_MULT_U, Residuo_DIV, Residuo_DIV_U, Resultado_ADD,
       Resultado_ADD_I, Resultado_AND, Resultado_AND_I, Resultado_NOR, Resultado_OR, Resultado_OR_I,
       Resultado_SLL, Resultado_SLLV, Resultado_SRA, Resultado_SRAV, Resultado_SRL, Resultado_SRLV,
       Resultado_SUB, Resultado_XOR, Resultado_XOR_I;

  assign bit_extender_1_out = {{2{1'b0}}, Direccion_Inmediata};  // Bit_Extender bit_extender_1
  Bit_Extender #(.in_width(32), .out_width(5), .\type ("zero")) bit_extender_2 (
    .in(Contenido_Registro_Fuente), .out(bit_extender_2_out));
  Shifter #(.width(28)) shifter_1 (.in(bit_extender_1_out), .\dist (5'b00010), .out(shifter_1_out));
  Adder #(.width(32)) adder_1 (.a(32'h4), .b(Indice_PC), .out(adder_1_out), .cin(1'b0), .cout(Overflow_Salto_J_JAL));
  assign Resultado_AND = Contenido_Registro_Fuente & Contenido_Registro_Objetivo;  // AND_Gate and_1, 32 bits wide
  assign Resultado_XOR = Contenido_Registro_Fuente ^ Contenido_Registro_Objetivo;  // XOR_Gate xor_1, 32 bits wide
  Shifter #(.width(32)) shifter_2 (
    .in(Contenido_Registro_Objetivo), .\dist (Cantidad_Corrimiento), .out(Resultado_SLL));
  Shifter #(.width(32)) shifter_3 (.in(Contenido_Registro_Objetivo), .\dist (bit_extender_2_out), .out(Resultado_SLLV));
  Shifter #(.shift("ar"), .width(32)) shifter_4 (
    .in(Contenido_Registro_Objetivo), .\dist (Cantidad_Corrimiento), .out(Resultado_SRA));
  assign Resultado_AND_I = Contenido_Registro_Fuente & Inmediato_Extendido_U;  // AND_Gate and_2, 32 bits wide
  assign Resultado_XOR_I = Contenido_Registro_Fuente ^ Inmediato_Extendido_U;  // XOR_Gate xor_2, 32 bits wide
  assign bit_extender_3_out = {{4{1'b0}}, shifter_1_out};  // Bit_Extender bit_extender_3
  assign and_3_out = 32'hf0000000 & adder_1_out;  // AND_Gate and_3, 32 bits wide
  assign Direccion_Salto_J_JAL = bit_extender_3_out | and_3_out;  // OR_Gate or_1, 32 bits wide
  Bit_Extender #(.in_width(32), .out_width(5), .\type ("zero")) bit_extender_4 (
    .in(Contenido_Registro_Fuente), .out(bit_extender_4_out));
  Bit_Extender #(.in_width(32), .out_width(5), .\type ("zero")) bit_extender_5 (
    .in(Contenido_Registro_Fuente), .out(bit_extender_5_out));
  assign Resultado_OR = Contenido_Registro_Fuente | Contenido_Registro_Objetivo;  // OR_Gate or_2, 32 bits wide
  assign Resultado_NOR = ~Resultado_OR;  // NOT_Gate not_1, 32 bits wide
  Shifter #(.shift("lr"), .width(32)) shifter_5 (
    .in(Contenido_Registro_Objetivo), .\dist (Cantidad_Corrimiento), .out(Resultado_SRL));
  Shifter #(.shift("ar"), .width(32)) shifter_6 (
    .in(Contenido_Registro_Objetivo), .\dist (bit_extender_5_out), .out(Resultado_SRAV));
  Shifter #(.shift("lr"), .width(32)) shifter_7 (
    .in(Contenido_Registro_Objetivo), .\dist (bit_extender_4_out), .out(Resultado_SRLV));
  assign Resultado_OR_I = Contenido_Registro_Fuente | Inmediato_Extendido_U;  // OR_Gate or_3, 32 bits wide
  assign Inmediato_Extendido = {{16{Valor_Inmediato[15]}}, Valor_Inmediato};  // Bit_Extender bit_extender_6
  assign Inmediato_Extendido_U = {{16{1'b0}}, Valor_Inmediato};  // Bit_Extender bit_extender_7
  Adder #(.width(32)) adder_2 (
    .a(Contenido_Registro_Fuente), .b(Contenido_Registro_Objetivo), .out(Resultado_ADD), .cin(1'b0),
    .cout(Overflow_ADD));
  Multiplier #(.mode("twosComplement"), .width(32)) multiplier_1 (
    .a(Contenido_Registro_Fuente), .b(Contenido_Registro_Objetivo), .out(Parte_Inferior_MULT),
    .cin({32{1'b0}}), .cout(Parte_Superior_MULT));
  Divider #(.mode("twosComplement"), .width(32)) divider_1 (
    .a(Contenido_Registro_Fuente), .b(Contenido_Registro_Objetivo), .out(Cociente_DIV), .upper({32{1'b0}}),
    .rem(Residuo_DIV));
  Adder #(.width(32)) adder_3 (
    .a(Contenido_Registro_Fuente), .b(Inmediato_Extendido), .out(Resultado_ADD_I), .cin(1'b0),
    .cout(Overflow_ADD_I));
  Subtractor #(.width(32)) subtractor_1 (
    .a(Contenido_Registro_Fuente), .b(Contenido_Registro_Objetivo), .out(Resultado_SUB), .bin(1'b0),
    .bout(Overflow_SUB));
  Multiplier #(.width(32)) multiplier_2 (
    .a(Contenido_Registro_Fuente), .b(Contenido_Registro_Objetivo), .out(Parte_Inferior_MULT_U),
    .cin({32{1'b0}}), .cout(Parte_Superior_MULT_U));
  Divider #(.width(32)) divider_2 (
    .a(Contenido_Registro_Fuente), .b(Contenido_Registro_Objetivo), .out(Cociente_DIV_U), .upper({32{1'b0}}),
    .rem(Residuo_DIV_U));
  // NoConnect on comparator_1_gt
  // NoConnect on comparator_1_eq
  Comparator #(.width(32)) comparator_1 (
    .a(Contenido_Registro_Fuente), .b(Inmediato_Extendido), .gt(comparator_1_gt), .eq(comparator_1_eq),
    .lt(Origen_Es_Menor_I));
  // NoConnect on comparator_2_gt
  // NoConnect on comparator_2_eq
  Comparator #(.mode("unsigned"), .width(32)) comparator_2 (
    .a(Contenido_Registro_Fuente), .b(Inmediato_Extendido), .gt(comparator_2_gt), .eq(comparator_2_eq),
    .lt(Origen_Es_Menor_I_U));
  Comparator #(.width(32)) comparator_3 (
    .a(Contenido_Registro_Fuente), .b(Contenido_Registro_Objetivo), .gt(Origen_Es_Mayor),
    .eq(Origen_Es_Igual), .lt(Origen_Es_Menor));
  // NoConnect on comparator_4_eq
  Comparator #(.mode("unsigned"), .width(32)) comparator_4 (
    .a(Contenido_Registro_Fuente), .b(Contenido_Registro_Objetivo), .gt(Origen_Es_Mayor_U),
    .eq(comparator_4_eq), .lt(Origen_Es_Menor_U));
  Multiplier #(.mode("twosComplement"), .width(16)) multiplier_3 (
    .a(Valor_Inmediato), .b(16'h4), .out(multiplier_3_out), .cin({16{1'b0}}), .cout(multiplier_3_cout));
  Adder #(.width(32)) adder_4 (
    .a({multiplier_3_cout, multiplier_3_out}), .b(Indice_PC), .out(adder_4_out), .cin(1'b0),
    .cout(adder_4_cout));
  Adder #(.width(32)) adder_5 (
    .a(32'h4), .b(adder_4_out), .out(Direccion_Salto_Condicional), .cin(1'b0), .cout(adder_5_cout));
  or or_4 (Overflow_Salto_Condicional, adder_5_cout, adder_4_cout);
  Adder #(.width(32)) adder_6 (
    .a(Indice_PC), .b(32'h8), .out(Direccion_Previo_Salto), .cin(1'b0), .cout(Overflow_Direccion_Previo_Salto));
  Bit_Extender #(.in_width(32), .out_width(2), .\type ("zero")) bit_extender_8 (
    .in(Direccion_Salto), .out(bit_extender_8_out));
  // NoConnect on bitfinder_1_index
  BitFinder #(.width(2)) bitfinder_1 (.in(bit_extender_8_out), .index(bitfinder_1_index), .found(Salto_Desalineado));

  // Other names for the same wires on the sheet: Direccion_Salto_JR_JALR[31:0] = Contenido_Registro_Fuente

  // Notes on the sheet:
  //   AND
  //   XOR
  //   SLL
  //   SLLV
  //   SRA
  //   AND_I
  //   XOR_I
  //   J, JAL
  //   Aritmética de bits
  //   Aritmética de bits
  //   Instrucciones de tipo R
  //   Instrucciones de tipo I
  //   Instrucciones de tipo J
  //   Direcciones de Memoria
  //   OR
  //   NOR
  //   SRL
  //   SRLV
  //   SRAV
  //   OR_I
  //   Extensiones
  //   ADD (U)
  //   MULT
  //   DIV
  //   ADD I (U)
  //   Arimética de enteros
  //   Arimética de enteros
  //   DIV U
  //   SUB (U)
  //   MULT U
  //   LTI
  //   Comparación de enteros
  //   LTI U
  //   LT, GT, EQ
  //   LT U, GT U
  //   Comparación de enteros
  //   BEQ, BNE, BLEZ, BGTZ
  //   Direcciones de Memoria
  //   JR, JALR
  //   Direcciones de Memoria
  //   JAL, JALR
endmodule
